# Fritzing sketch 1.1_Board (saved by Fritzing 1.0.6)
breadboards: 1

parts:
  A1 = Arduino UNO R4 WiFi
  DHT1 = DHT22 Humidity and Temperature Sensor
  Part1 = KY-037 High Sensitivity Sound Detection Module [package="Breakout board"]
  Componente1 = MQ-7 breakout
  Componente2 = BH1750
  Componente3 = InvenSense MPU6050
  ESP32_-_Front1 = ESP32 - CAM  # not connected
  Raspberry_Pi_1 = Raspberry Pi 4 [part_number=RPI-4-b]  # not connected

nets:
  GND: A1.Pin_2, A1.Pin_9, A1.Pin_10, A1.Pin_48, DHT1.GND, Part1.G, Componente1.GND, Componente2.GND, Componente3.GND
  N1: A1.Pin_7, Componente3.VCC
  VCC: A1.Pin_8, DHT1.VDD, Part1.+, Componente1.VCC, Componente2.VCC
  N2: A1.Pin_12, Part1.A0
  N3: A1.Pin_13, Componente1.AO
  N4: A1.Pin_36, DHT1.DATA
  N5: A1.Pin_50, Componente2.SDA, Componente3.SDA
  N6: A1.Pin_51, Componente2.SCL, Componente3.XDA

custom parts:
  Arduino UNO R4 WiFi: The Arduino UNO R4 WiFi merges the RA4M1 microprocessor from Renesas with the ESP32-S3 from Espressif, creating an all-in-one tool for makers with enhanced processing power and a diverse array of new peripherals.
  KY-037 High Sensitivity Sound Detection Module: KY-037 high sensitivity sound detection module is an analog/digital sensor that uses a condenser microphone to observe changes in environment noise.
  MQ-7 breakout: SKU: 101282
  BH1750: Light Sensor
  ESP32 - CAM: The ESP32-CAM has a very competitive small-size camera module that can operate independently as a minimum system with a footprint of only 27*40.5*4.5mm and a deep sleep current of up to 6mA.
  Raspberry Pi 4: The RPi4, a faster version of the awesome Raspberry Pi 2 B ARM Board with 40 pin gpio. Ready for special Raspberry Pi B+ and RPi2 Hat (Hardware attached (on) top)
